# Fritzing sketch EarthWear (saved by Fritzing 0.9.7b)
breadboards: 1

parts:
  Teensy1 = Teensy 4.1
  Part1 = Adafruit MAX98357A I2S 3W Class D Amplifier [part_number="Adafruit #3006"]
  R2 = Resistor [tolerance=±5% power=0.25 resistance=220 package=THT]
  PIR1 = PIR sensor
  PIR2 = PIR sensor
  SP1 = SPEAKER [package=pcb_mount_speaker]
  Part2 = Adafruit MAX98357A I2S 3W Class D Amplifier [part_number="Adafruit #3006"]
  R3 = Resistor [tolerance=±5% power=0.25 resistance=220 package=THT]
  SP2 = SPEAKER [package=pcb_mount_speaker]

nets:
  GND: Teensy1.GND, Teensy1.GND2#55, PIR1.GND, PIR2.GND
  N1: Teensy1.D7, Part1.DIN, Part2.DIN
  N2: Teensy1.A3/D17, PIR2.SIG
  N3: Teensy1.A4/D18, PIR1.SIG
  N4: Teensy1.A6/D20, Part1.LRCLK, Part2.LRCLK
  N5: Teensy1.A7/D21, Part1.BCLK, Part2.BCLK
  VDD: Teensy1.3V3_LOW, PIR1.VDD, PIR2.VDD
  GND_2: Teensy1.GND2#31, Part1.GND, R2.Pin_1, Part2.GND, R3.Pin_1
  VIN: Teensy1.Vin, Part1.VIN, Part2.VIN
  N6: Part1.GAIN, R2.Pin_0
  N7: Part1.VO-, SP1.+
  N8: Part1.VO+, SP1.-
  N9: Part2.GAIN, R3.Pin_0
  N10: Part2.VO-, SP2.+
  N11: Part2.VO+, SP2.-

notes:
  3.3V
  5V/USB
  100 kΩ
  Bone transducer and amps are identical and share signal

custom parts:
  Teensy 4.1: The Teensy is a complete USB-based microcontoller development system, in a very small footprint, capable of implementing many types of projects. All programming is done via the USB port. No special programmer is needed, only a standard micro-USB cable and a PC or Macintosh with a USB port.
  Adafruit MAX98357A I2S 3W Class D Amplifier: Listen to this good news - we now have an all in one digital audio amp breakout board that works incredibly well with the Raspberry Pi! If you're looking for an easy and low cost way to get you digital sound files bumpin' then the MAX08357 I2S Amp Breakout is for you. It takes standard I2S digital audio input and, not only decodes it into analog, but also amplifies it directly into a speaker.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
